// Logisim project branch-comp.circ as structural Verilog: 1 circuit, main circuit branch_comp
module branch_comp (
  input  [31:0] BrData1,
  input  [31:0] BrData2,
  input  BrUn,
  output BrEq,
  output BrLt
);

  wire comparator_2_lt, comparator_3_lt;

  Comparator #(.width(32)) comparator_1 (.a(BrData1), .b(BrData2), .eq(BrEq));  // open: gt, lt
  Comparator #(.width(32)) comparator_2 (.a(BrData1), .b(BrData2), .lt(comparator_2_lt));  // open: gt, eq
  Comparator #(.mode("unsigned"), .width(32)) comparator_3 (
    .a(BrData1), .b(BrData2), .lt(comparator_3_lt));  // open: gt, eq
  Multiplexer multiplexer_1 (.in0(comparator_2_lt), .in1(comparator_3_lt), .out(BrLt), .sel(BrUn));

  // Notes on the sheet:
  //   INPUTS to your circuit
  //   beq rs1 rs2 offset / bne rs1 rs2 offset
  //   DON'T CHANGE THE LOCATIONS OF THE INPUTS AND OUTPUTS!
  //   OUTPUT from your circuit
endmodule
