// Logisim project control-logic.circ as structural Verilog: 1 circuit, main circuit control_logic
module control_logic (
  input  [31:0] Instruction,
  input  BrEq,
  input  BrLt,
  output PCSel,
  output RegWEn,
  output [2:0] ImmSel,
  output BrUn,
  output ASel,
  output BSel,
  output [3:0] ALUSel,
  output MemRW,
  output [1:0] WBSel
);

  wire add, addi, and_2_out, and_5_out, and_6_out, and_18_out, and_19_out, and_20_out, and_21_out,
       and_22_out, and_23_out, and_24_out, and_25_out, and_26_out, and_27_out, and_28_out, and_29_out,
       and_42_out, and_43_out, and_44_out, and_45_out, and_ctrl, andi, auipc, B_type, beq, bge, bgeu, blt,
       bltu, bne, comparator_8_eq, comparator_9_eq, comparator_10_eq, comparator_11_eq, comparator_12_eq,
       comparator_13_eq, comparator_14_eq, comparator_15_eq, comparator_16_eq, comparator_17_eq,
       comparator_18_eq, comparator_19_eq, comparator_20_eq, comparator_21_eq, comparator_22_eq,
       comparator_23_eq, comparator_24_eq, comparator_25_eq, comparator_26_eq, comparator_27_eq,
       comparator_28_eq, comparator_29_eq, comparator_30_eq, comparator_31_eq, comparator_32_eq,
       comparator_33_eq, comparator_34_eq, comparator_35_eq, comparator_36_eq, comparator_37_eq,
       comparator_38_eq, comparator_39_eq, comparator_40_eq, comparator_41_eq, comparator_42_eq,
       comparator_43_eq, comparator_44_eq, comparator_45_eq, comparator_46_eq, comparator_47_eq,
       comparator_48_eq, comparator_49_eq, comparator_50_eq, comparator_51_eq, comparator_52_eq,
       comparator_53_eq, comparator_54_eq, comparator_55_eq, I_type, I_type_imm, I_type_jump, jal, jalr, lb,
       lh, lui, lw, mul, mulh, mulhu, not_1_out, not_2_out, or_1_out, or_2_out, or_3_out, or_4_out, or_5_out,
       or_6_out, or_ctrl, ori, R_type, S_type, sb, sh, sll_ctrl, slli, slt, slti, sra_ctrl, srai, srl_ctrl,
       srli, sub, sw, xor_ctrl, xori;
  wire [5:0] encoder;
  wire [15:14] ROM_1_data;

  Comparator #(.width(7)) comparator_1 (.a(7'b0000011), .b(Instruction[6:0]), .eq(I_type));  // open: gt, lt
  Comparator #(.width(7)) comparator_2 (.a(7'b0010011), .b(Instruction[6:0]), .eq(I_type_imm));  // open: gt, lt
  Comparator #(.width(7)) comparator_3 (.a(7'b1100111), .b(Instruction[6:0]), .eq(I_type_jump));  // open: gt, lt
  Comparator #(.width(7)) comparator_4 (.a(7'b0110011), .b(Instruction[6:0]), .eq(R_type));  // open: gt, lt
  Comparator #(.width(7)) comparator_5 (.a(7'b1100011), .b(Instruction[6:0]), .eq(B_type));  // open: gt, lt
  Comparator #(.width(7)) comparator_6 (.a(7'b1101111), .b(Instruction[6:0]), .eq(jal));  // open: gt, lt
  Comparator #(.width(7)) comparator_7 (.a(7'b0100011), .b(Instruction[6:0]), .eq(S_type));  // open: gt, lt
  ROM #(.addrWidth(6), .dataWidth(16)) ROM_1 (
    .addr(encoder), .data({ROM_1_data, WBSel, MemRW, ALUSel, BSel, ASel, BrUn, ImmSel, RegWEn}));
  Comparator #(.width(3)) comparator_8 (.a(3'b000), .b(Instruction[14:12]), .eq(comparator_8_eq));  // open: gt, lt
  Comparator #(.width(3)) comparator_9 (.a(3'b001), .b(Instruction[14:12]), .eq(comparator_9_eq));  // open: gt, lt
  Comparator #(.width(7)) comparator_10 (.a({7{1'b0}}), .b(Instruction[31:25]), .eq(comparator_10_eq));  // open: gt, lt
  Comparator #(.width(3)) comparator_11 (.a(3'b010), .b(Instruction[14:12]), .eq(comparator_11_eq));  // open: gt, lt
  Comparator #(.width(3)) comparator_12 (.a(3'b100), .b(Instruction[14:12]), .eq(comparator_12_eq));  // open: gt, lt
  Comparator #(.width(3)) comparator_13 (.a(3'b101), .b(Instruction[14:12]), .eq(comparator_13_eq));  // open: gt, lt
  Comparator #(.width(7)) comparator_14 (.a({7{1'b0}}), .b(Instruction[31:25]), .eq(comparator_14_eq));  // open: gt, lt
  Comparator #(.width(3)) comparator_15 (.a(3'b101), .b(Instruction[14:12]), .eq(comparator_15_eq));  // open: gt, lt
  Comparator #(.width(7)) comparator_16 (
    .a(7'b0100000), .b(Instruction[31:25]), .eq(comparator_16_eq));  // open: gt, lt
  Comparator #(.width(3)) comparator_17 (.a(3'b110), .b(Instruction[14:12]), .eq(comparator_17_eq));  // open: gt, lt
  Comparator #(.width(3)) comparator_18 (.a(3'b111), .b(Instruction[14:12]), .eq(comparator_18_eq));  // open: gt, lt
  Comparator #(.width(3)) comparator_19 (.a(3'b000), .b(Instruction[14:12]), .eq(comparator_19_eq));  // open: gt, lt
  Comparator #(.width(3)) comparator_20 (.a(3'b001), .b(Instruction[14:12]), .eq(comparator_20_eq));  // open: gt, lt
  Comparator #(.width(3)) comparator_21 (.a(3'b100), .b(Instruction[14:12]), .eq(comparator_21_eq));  // open: gt, lt
  Comparator #(.width(3)) comparator_22 (.a(3'b101), .b(Instruction[14:12]), .eq(comparator_22_eq));  // open: gt, lt
  Comparator #(.width(3)) comparator_23 (.a(3'b110), .b(Instruction[14:12]), .eq(comparator_23_eq));  // open: gt, lt
  Comparator #(.width(3)) comparator_24 (.a(3'b111), .b(Instruction[14:12]), .eq(comparator_24_eq));  // open: gt, lt
  and and_1 (addi, I_type_imm, comparator_8_eq);
  and and_2 (and_2_out, comparator_9_eq, comparator_10_eq);
  and and_3 (slti, I_type_imm, comparator_11_eq);
  and and_4 (xori, I_type_imm, comparator_12_eq);
  and and_5 (and_5_out, comparator_13_eq, comparator_14_eq);
  and and_6 (and_6_out, comparator_15_eq, comparator_16_eq);
  and and_7 (ori, I_type_imm, comparator_17_eq);
  and and_8 (andi, I_type_imm, comparator_18_eq);
  and and_9 (beq, B_type, comparator_19_eq);
  and and_10 (bne, B_type, comparator_20_eq);
  and and_11 (blt, B_type, comparator_21_eq);
  and and_12 (bge, B_type, comparator_22_eq);
  and and_13 (bltu, B_type, comparator_23_eq);
  and and_14 (bgeu, B_type, comparator_24_eq);
  and and_15 (slli, I_type_imm, and_2_out);
  and and_16 (srli, I_type_imm, and_5_out);
  and and_17 (srai, I_type_imm, and_6_out);
  Priority_Encoder #(.select_enc(6)) priority_encoder_1 (
    .in0(add), .in1(mul), .in2(sub), .in3(sll_ctrl), .in4(mulh), .in5(mulhu), .in6(slt), .in7(xor_ctrl),
    .in8(srl_ctrl), .in9(sra_ctrl), .in10(or_ctrl), .in11(and_ctrl), .in12(lb), .in13(lh), .in14(lw),
    .in15(addi), .in16(slli), .in17(slti), .in18(xori), .in19(srli), .in20(srai), .in21(ori), .in22(andi),
    .in23(sb), .in24(sh), .in25(sw), .in26(beq), .in27(bne), .in28(blt), .in29(bge), .in30(bltu),
    .in31(bgeu), .in32(auipc), .in33(lui), .in34(jal), .in35(jalr), .out(encoder));  // open: in36, in37, in38, in39, in40, in41, in42, in43, in44, in45, in46, in47, in48, in49, in50, in51, in52, in53, in54, in55, in56, in57, in58, in59, in60, in61, in62, in63, gs, en_out, en_in
  Comparator #(.width(3)) comparator_25 (.a(3'b000), .b(Instruction[14:12]), .eq(comparator_25_eq));  // open: gt, lt
  Comparator #(.width(7)) comparator_26 (.a({7{1'b0}}), .b(Instruction[31:25]), .eq(comparator_26_eq));  // open: gt, lt
  Comparator #(.width(3)) comparator_27 (.a(3'b000), .b(Instruction[14:12]), .eq(comparator_27_eq));  // open: gt, lt
  Comparator #(.width(7)) comparator_28 (
    .a(7'b0100000), .b(Instruction[31:25]), .eq(comparator_28_eq));  // open: gt, lt
  Comparator #(.width(3)) comparator_29 (.a(3'b111), .b(Instruction[14:12]), .eq(comparator_29_eq));  // open: gt, lt
  Comparator #(.width(7)) comparator_30 (.a({7{1'b0}}), .b(Instruction[31:25]), .eq(comparator_30_eq));  // open: gt, lt
  Comparator #(.width(3)) comparator_31 (.a(3'b110), .b(Instruction[14:12]), .eq(comparator_31_eq));  // open: gt, lt
  Comparator #(.width(7)) comparator_32 (.a({7{1'b0}}), .b(Instruction[31:25]), .eq(comparator_32_eq));  // open: gt, lt
  Comparator #(.width(3)) comparator_33 (.a(3'b100), .b(Instruction[14:12]), .eq(comparator_33_eq));  // open: gt, lt
  Comparator #(.width(7)) comparator_34 (.a({7{1'b0}}), .b(Instruction[31:25]), .eq(comparator_34_eq));  // open: gt, lt
  Comparator #(.width(3)) comparator_35 (.a(3'b001), .b(Instruction[14:12]), .eq(comparator_35_eq));  // open: gt, lt
  Comparator #(.width(7)) comparator_36 (.a({7{1'b0}}), .b(Instruction[31:25]), .eq(comparator_36_eq));  // open: gt, lt
  Comparator #(.width(3)) comparator_37 (.a(3'b101), .b(Instruction[14:12]), .eq(comparator_37_eq));  // open: gt, lt
  Comparator #(.width(7)) comparator_38 (.a({7{1'b0}}), .b(Instruction[31:25]), .eq(comparator_38_eq));  // open: gt, lt
  Comparator #(.width(3)) comparator_39 (.a(3'b101), .b(Instruction[14:12]), .eq(comparator_39_eq));  // open: gt, lt
  Comparator #(.width(7)) comparator_40 (
    .a(7'b0100000), .b(Instruction[31:25]), .eq(comparator_40_eq));  // open: gt, lt
  Comparator #(.width(3)) comparator_41 (.a(3'b010), .b(Instruction[14:12]), .eq(comparator_41_eq));  // open: gt, lt
  Comparator #(.width(7)) comparator_42 (.a({7{1'b0}}), .b(Instruction[31:25]), .eq(comparator_42_eq));  // open: gt, lt
  Comparator #(.width(3)) comparator_43 (.a(3'b000), .b(Instruction[14:12]), .eq(comparator_43_eq));  // open: gt, lt
  Comparator #(.width(7)) comparator_44 (
    .a(7'b0000001), .b(Instruction[31:25]), .eq(comparator_44_eq));  // open: gt, lt
  Comparator #(.width(3)) comparator_45 (.a(3'b001), .b(Instruction[14:12]), .eq(comparator_45_eq));  // open: gt, lt
  Comparator #(.width(7)) comparator_46 (
    .a(7'b0000001), .b(Instruction[31:25]), .eq(comparator_46_eq));  // open: gt, lt
  Comparator #(.width(3)) comparator_47 (.a(3'b011), .b(Instruction[14:12]), .eq(comparator_47_eq));  // open: gt, lt
  Comparator #(.width(7)) comparator_48 (
    .a(7'b0000001), .b(Instruction[31:25]), .eq(comparator_48_eq));  // open: gt, lt
  and and_18 (and_18_out, comparator_25_eq, comparator_26_eq);
  and and_19 (and_19_out, comparator_27_eq, comparator_28_eq);
  and and_20 (and_20_out, comparator_29_eq, comparator_30_eq);
  and and_21 (and_21_out, comparator_31_eq, comparator_32_eq);
  and and_22 (and_22_out, comparator_33_eq, comparator_34_eq);
  and and_23 (and_23_out, comparator_35_eq, comparator_36_eq);
  and and_24 (and_24_out, comparator_37_eq, comparator_38_eq);
  and and_25 (and_25_out, comparator_39_eq, comparator_40_eq);
  and and_26 (and_26_out, comparator_41_eq, comparator_42_eq);
  and and_27 (and_27_out, comparator_43_eq, comparator_44_eq);
  and and_28 (and_28_out, comparator_45_eq, comparator_46_eq);
  and and_29 (and_29_out, comparator_47_eq, comparator_48_eq);
  and and_30 (add, R_type, and_18_out);
  and and_31 (sub, R_type, and_19_out);
  and and_32 (and_ctrl, R_type, and_20_out);
  and and_33 (or_ctrl, R_type, and_21_out);
  and and_34 (xor_ctrl, R_type, and_22_out);
  and and_35 (sll_ctrl, R_type, and_23_out);
  and and_36 (srl_ctrl, R_type, and_24_out);
  and and_37 (sra_ctrl, R_type, and_25_out);
  and and_38 (slt, R_type, and_26_out);
  and and_39 (mul, R_type, and_27_out);
  and and_40 (mulh, R_type, and_28_out);
  and and_41 (mulhu, R_type, and_29_out);
  not not_1 (not_1_out, BrLt);
  or or_1 (or_1_out, bge, bgeu);
  or or_2 (or_2_out, blt, bltu);
  and and_42 (and_42_out, not_1_out, or_1_out);
  and and_43 (and_43_out, or_2_out, BrLt);
  or or_3 (or_3_out, and_42_out, and_43_out);
  not not_2 (not_2_out, BrEq);
  and and_44 (and_44_out, bne, not_2_out);
  Comparator #(.width(3)) comparator_49 (.a(3'b000), .b(Instruction[14:12]), .eq(comparator_49_eq));  // open: gt, lt
  Comparator #(.width(3)) comparator_50 (.a(3'b001), .b(Instruction[14:12]), .eq(comparator_50_eq));  // open: gt, lt
  Comparator #(.width(3)) comparator_51 (.a(3'b010), .b(Instruction[14:12]), .eq(comparator_51_eq));  // open: gt, lt
  Comparator #(.width(3)) comparator_52 (.a(3'b000), .b(Instruction[14:12]), .eq(comparator_52_eq));  // open: gt, lt
  Comparator #(.width(3)) comparator_53 (.a(3'b001), .b(Instruction[14:12]), .eq(comparator_53_eq));  // open: gt, lt
  Comparator #(.width(3)) comparator_54 (.a(3'b010), .b(Instruction[14:12]), .eq(comparator_54_eq));  // open: gt, lt
  or or_4 (or_4_out, and_44_out, or_3_out);
  and and_45 (and_45_out, beq, BrEq);
  and and_46 (lb, I_type, comparator_49_eq);
  and and_47 (lh, I_type, comparator_50_eq);
  and and_48 (lw, I_type, comparator_51_eq);
  and and_49 (sb, S_type, comparator_52_eq);
  and and_50 (sh, S_type, comparator_53_eq);
  and and_51 (sw, S_type, comparator_54_eq);
  or or_5 (or_5_out, or_4_out, and_45_out);
  or or_6 (or_6_out, jal, jalr);
  or or_7 (PCSel, or_6_out, or_5_out);
  Comparator #(.width(3)) comparator_55 (.a(3'b000), .b(Instruction[14:12]), .eq(comparator_55_eq));  // open: gt, lt
  Comparator #(.width(7)) comparator_56 (.a(7'b0010111), .b(Instruction[6:0]), .eq(auipc));  // open: gt, lt
  and and_52 (jalr, I_type_jump, comparator_55_eq);
  Comparator #(.width(7)) comparator_57 (.a(7'b0110111), .b(Instruction[6:0]), .eq(lui));  // open: gt, lt

  // Other names for the same wires on the sheet: opcode[6:0] = Instruction[6:0]; funct3[2:0] = Instruction[14:12];
  //   funct7[6:0] = Instruction[31:25]

  // Notes on the sheet:
  //   INPUTS to your circuit
  //   contents of ROM_1 (hex, n*v repeats v):
  //   1001 1401 1601 1081 1481 1581 1101 1201 1281 1681 1301 1381 41 41 41 1041 10c1 1141 1241 12c1 16c1
  //   1341 13c1 842 842 842 4*64 74 74 1067 17e7 2069 2041
  //   ROM FOR CONTROL LOGIC
  //   DON'T CHANGE THE LOCATIONS OF THE INPUTS AND OUTPUTS!
  //   This is only if you choose to do the ROM option
  //   B-Type Instructions
  //   OUTPUT from your circuit
  //   I-Type Instructions
  //   R-Type Instructions
  //   Reminder: If using ROM, use combinational logic for PCSel
  //   Load & Store Instructions
  //   Jump Instructions
endmodule
