// Logisim project cpu.circ as structural Verilog: 1 circuit, main circuit cpu
module cpu (
  input  clk,
  input  [31:0] Instruction,
  input  [31:0] MemReadData,
  output [31:0] MemAddress,
  output [31:0] ProgramCounter,
  output [31:0] ra,
  output [31:0] sp,
  output [31:0] t0,
  output [31:0] t1,
  output [31:0] t2,
  output [31:0] s0,
  output [31:0] s1,
  output [31:0] a0,
  output [3:0] MemWriteMask,
  output [31:0] MemWriteData
);

  wire asel, breq, brlt, brun, bsel, memrw, pcsel, RegWen;
  wire [1:0] wbsel;
  wire [2:0] funct3, immsel;
  wire [3:0] alusel;
  wire [31:0] adder_1_out, immediate, Instruction_Hazard, multiplexer_1_out, multiplexer_2_out,
       multiplexer_3_out, multiplexer_4_out, PC_4, pipeline, ReadData1, ReadData2, Write_Result, Write_To_Mem;

  Adder #(.width(32)) adder_1 (.a(ProgramCounter), .b(32'h4), .out(adder_1_out));  // open: cin, cout
  Multiplexer #(.width(32)) multiplexer_1 (.in0(adder_1_out), .in1(MemAddress), .out(multiplexer_1_out), .sel(pcsel));
  Register #(.width(32)) PC (.D(multiplexer_1_out), .en(1'b1), .clk(clk), .Q(ProgramCounter));  // open: clr
  Adder #(.width(32)) adder_2 (.a(pipeline), .b(32'h4), .out(PC_4));  // open: cin, cout
  Register #(.width(32)) register_1 (.D(ProgramCounter), .en(1'b1), .clk(clk), .Q(pipeline));  // open: clr
  Multiplexer #(.width(32)) multiplexer_2 (.in0(Instruction), .in1(32'h13), .out(multiplexer_2_out), .sel(pcsel));
  Register #(.width(32)) register_2 (
    .D(multiplexer_2_out), .clk(clk), .Q({Instruction_Hazard[31:15], funct3, Instruction_Hazard[11:0]}));  // open: en, clr
  control_logic control_logic_1 (
    .Instruction({Instruction_Hazard[31:15], funct3, Instruction_Hazard[11:0]}), .BrEq(breq), .BrLt(brlt),
    .PCSel(pcsel), .RegWEn(RegWen), .ImmSel(immsel), .BrUn(brun), .ASel(asel), .BSel(bsel), .ALUSel(alusel),
    .MemRW(memrw), .WBSel(wbsel));
  regfile regfile_1 (
    .ReadIndex1(Instruction_Hazard[19:15]), .ReadIndex2(Instruction_Hazard[24:20]),
    .WriteIndex(Instruction_Hazard[11:7]), .WriteData(Write_Result), .RegWEn(RegWen), .clk(clk), .ra(ra),
    .sp(sp), .t0(t0), .t1(t1), .t2(t2), .s0(s0), .s1(s1), .a0(a0), .ReadData1(ReadData1),
    .ReadData2(ReadData2));
  imm_gen imm_gen_1 (
    .Instruction({Instruction_Hazard[31:15], funct3, Instruction_Hazard[11:0]}), .ImmSel(immsel),
    .Immediate(immediate));
  branch_comp branch_comp_1 (.BrData1(ReadData1), .BrData2(ReadData2), .BrUn(brun), .BrEq(breq), .BrLt(brlt));
  Multiplexer #(.width(32)) multiplexer_3 (.in0(ReadData1), .in1(pipeline), .out(multiplexer_3_out), .sel(asel));
  Multiplexer #(.width(32)) multiplexer_4 (.in0(ReadData2), .in1(immediate), .out(multiplexer_4_out), .sel(bsel));
  alu alu_1 (.A(multiplexer_3_out), .B(multiplexer_4_out), .ALUSel(alusel), .ALUResult(MemAddress));
  Multiplexer #(.select(2), .width(32)) multiplexer_5 (
    .in0(Write_To_Mem), .in1(MemAddress), .in2(PC_4), .in3(immediate), .out(Write_Result), .sel(wbsel));
  partial_store partial_store_1 (
    .Instruction({Instruction_Hazard[31:15], funct3, Instruction_Hazard[11:0]}), .MemAddress(MemAddress),
    .DataFromReg(ReadData2), .MemRW(memrw), .MemWriteMask(MemWriteMask), .DataToMem(MemWriteData));
  partial_load partial_load_1 (
    .Instruction({Instruction_Hazard[31:15], funct3, Instruction_Hazard[11:0]}), .MemAddress(MemAddress),
    .DataFromMem(MemReadData), .DataToReg(Write_To_Mem));

  // Other names for the same wires on the sheet: opcode[6:0] = Instruction_Hazard[6:0];
  //   rd[4:0] = Instruction_Hazard[11:7]; Instruction_Hazard[14:12] = funct3; rs1[4:0] = Instruction_Hazard[19:15];
  //   rs2[4:0] = Instruction_Hazard[24:20]; WriteData[31:0] = MemAddress

  // Notes on the sheet:
  //   splittling -- part 1
  //   To IMEM
  //   IMEM (do **NOT** move this)
  //   From IMEM
  //   Inputs/Outputs for testing. Do **NOT** move these.
  //   It is OK to move the PC, RegFile, ALU, MEM, Branch Comp, Imm Gen, Partial Load, Partial Store and Control Logic to wherever is most convenient for you when constructing your CPU, and to delete this text
  //   To DMEM
  //   DMEM (do **NOT** move this)
  //   From DMEM
endmodule
