// Logisim project partial-store.circ as structural Verilog: 1 circuit, main circuit partial_store
module partial_store (
  input  [31:0] Instruction,
  input  [31:0] MemAddress,
  input  [31:0] DataFromReg,
  input  MemRW,
  output [3:0] MemWriteMask,
  output [31:0] DataToMem
);

  wire [3:0] mem_write_func, store_byte_mw, store_half_mw;
  wire [31:0] store_byte, store_byte_00, store_byte_01, store_byte_10, store_byte_11, store_half_word,
       store_half_word_00, store_half_word_10;

  Shifter #(.width(32)) shifter_1 (.in(store_byte_00), .\dist (5'b01000), .out(store_byte_01));
  Shifter #(.width(32)) shifter_2 (.in(store_byte_00), .\dist (5'b10000), .out(store_byte_10));
  Shifter #(.width(32)) shifter_3 (.in(store_byte_00), .\dist (5'b11000), .out(store_byte_11));
  assign store_byte_00 = {{24{1'b0}}, DataFromReg[7:0]};  // Bit_Extender bit_extender_1
  Multiplexer #(.width(32)) multiplexer_1 (
    .in0(store_half_word_00), .in1(store_half_word_10), .out(store_half_word), .sel(MemAddress[1]));
  Multiplexer #(.select(2), .width(32)) multiplexer_2 (
    .in0(store_byte_00), .in1(store_byte_01), .in2(store_byte_10), .in3(store_byte_11), .out(store_byte),
    .sel(MemAddress[1:0]));
  Shifter #(.width(32)) shifter_4 (.in(store_half_word_00), .\dist (5'b10000), .out(store_half_word_10));
  Multiplexer #(.select(2), .width(32)) multiplexer_3 (
    .in0(store_byte), .in1(store_half_word), .in2(DataFromReg), .out(DataToMem), .sel(Instruction[13:12]));  // open: in3
  Multiplexer #(.select(2), .width(4)) multiplexer_4 (
    .in0(4'b0001), .in1(4'b0010), .in2(4'b0100), .in3(4'b1000), .out(store_byte_mw), .sel(MemAddress[1:0]));
  Multiplexer #(.width(4)) multiplexer_5 (.in0(4'b0011), .in1(4'b1100), .out(store_half_mw), .sel(MemAddress[1]));
  Multiplexer #(.select(2), .width(4)) multiplexer_6 (
    .in0(store_byte_mw), .in1(store_half_mw), .in2(4'b1111), .out(mem_write_func), .sel(Instruction[13:12]));  // open: in3
  assign store_half_word_00 = {{16{1'b0}}, DataFromReg[15:0]};  // Bit_Extender bit_extender_2
  Multiplexer #(.width(4)) multiplexer_7 (.in0(4'b0000), .in1(mem_write_func), .out(MemWriteMask), .sel(MemRW));

  // Other names for the same wires on the sheet: funct3[1:0] = Instruction[13:12];
  //   bottom_2_bits[1:0] = MemAddress[1:0]; store_word[31:0] = DataFromReg

  // Notes on the sheet:
  //   INPUTS to your circuit
  //   DON'T CHANGE THE LOCATIONS OF THE INPUTS AND OUTPUTS!
  //   MemWrite Muxes
  //   OUTPUT from your circuit
endmodule
