// Logisim project regfile.circ as structural Verilog: 1 circuit, main circuit regfile
module regfile (
  input  [4:0] ReadIndex1,
  input  [4:0] ReadIndex2,
  input  [4:0] WriteIndex,
  input  [31:0] WriteData,
  input  RegWEn,
  input  clk,
  output [31:0] ra,
  output [31:0] sp,
  output [31:0] t0,
  output [31:0] t1,
  output [31:0] t2,
  output [31:0] s0,
  output [31:0] s1,
  output [31:0] a0,
  output [31:0] ReadData1,
  output [31:0] ReadData2
);

  wire r1, r2, r3, r4, r5, r6, r7, r8, r9, r10, r11, r12, r13, r14, r15, r16, r17, r18, r19, r20, r21, r22,
       r23, r24, r25, r26, r27, r28, r29, r30, r31;
  wire [31:0] x3, x4, x11, x12, x13, x14, x15, x16, x17, x18, x19, x20, x21, x22, x23, x24, x25, x26, x27,
       x28, x29, x30, x31;

  Register #(.width(32)) register_1 (.D(WriteData), .en(r1), .clk(clk), .Q(ra));  // open: clr
  Register #(.width(32)) register_2 (.D(WriteData), .en(r2), .clk(clk), .Q(sp));  // open: clr
  Register #(.width(32)) register_3 (.D(WriteData), .en(r3), .clk(clk), .Q(x3));  // open: clr
  Register #(.width(32)) register_4 (.D(WriteData), .en(r4), .clk(clk), .Q(x4));  // open: clr
  Register #(.width(32)) register_5 (.D(WriteData), .en(r5), .clk(clk), .Q(t0));  // open: clr
  Register #(.width(32)) register_6 (.D(WriteData), .en(r6), .clk(clk), .Q(t1));  // open: clr
  Register #(.width(32)) register_7 (.D(WriteData), .en(r7), .clk(clk), .Q(t2));  // open: clr
  Register #(.width(32)) register_8 (.D(WriteData), .en(r8), .clk(clk), .Q(s0));  // open: clr
  Register #(.width(32)) register_9 (.D(WriteData), .en(r9), .clk(clk), .Q(s1));  // open: clr
  Register #(.width(32)) register_10 (.D(WriteData), .en(r10), .clk(clk), .Q(a0));  // open: clr
  Register #(.width(32)) register_11 (.D(WriteData), .en(r11), .clk(clk), .Q(x11));  // open: clr
  Register #(.width(32)) register_12 (.D(WriteData), .en(r12), .clk(clk), .Q(x12));  // open: clr
  Register #(.width(32)) register_13 (.D(WriteData), .en(r13), .clk(clk), .Q(x13));  // open: clr
  Register #(.width(32)) register_14 (.D(WriteData), .en(r14), .clk(clk), .Q(x14));  // open: clr
  Register #(.width(32)) register_15 (.D(WriteData), .en(r15), .clk(clk), .Q(x15));  // open: clr
  Register #(.width(32)) register_16 (.D(WriteData), .en(r16), .clk(clk), .Q(x16));  // open: clr
  Register #(.width(32)) register_17 (.D(WriteData), .en(r17), .clk(clk), .Q(x17));  // open: clr
  Register #(.width(32)) register_18 (.D(WriteData), .en(r18), .clk(clk), .Q(x18));  // open: clr
  Register #(.width(32)) register_19 (.D(WriteData), .en(r19), .clk(clk), .Q(x19));  // open: clr
  Register #(.width(32)) register_20 (.D(WriteData), .en(r21), .clk(clk), .Q(x20));  // open: clr
  Register #(.width(32)) register_21 (.D(WriteData), .en(r23), .clk(clk), .Q(x23));  // open: clr
  Register #(.width(32)) register_22 (.D(WriteData), .en(r24), .clk(clk), .Q(x24));  // open: clr
  Register #(.width(32)) register_23 (.D(WriteData), .en(r25), .clk(clk), .Q(x25));  // open: clr
  Register #(.width(32)) register_24 (.D(WriteData), .en(r26), .clk(clk), .Q(x26));  // open: clr
  Register #(.width(32)) register_25 (.D(WriteData), .en(r27), .clk(clk), .Q(x27));  // open: clr
  Register #(.width(32)) register_26 (.D(WriteData), .en(r28), .clk(clk), .Q(x28));  // open: clr
  Register #(.width(32)) register_27 (.D(WriteData), .en(r29), .clk(clk), .Q(x29));  // open: clr
  Register #(.width(32)) register_28 (.D(WriteData), .en(r30), .clk(clk), .Q(x30));  // open: clr
  Register #(.width(32)) register_29 (.D(WriteData), .en(r31), .clk(clk), .Q(x31));  // open: clr
  Register #(.width(32)) register_30 (.D(WriteData), .en(r22), .clk(clk), .Q(x22));  // open: clr
  Multiplexer #(.select(5), .width(32)) multiplexer_1 (
    .in0({32{1'b0}}), .in1(ra), .in2(sp), .in3(x3), .in4(x4), .in5(t0), .in6(t1), .in7(t2), .in8(s0),
    .in9(s1), .in10(a0), .in11(x11), .in12(x12), .in13(x13), .in14(x14), .in15(x15), .in16(x16), .in17(x17),
    .in18(x18), .in19(x19), .in20(x20), .in21(x21), .in22(x22), .in23(x23), .in24(x24), .in25(x25),
    .in26(x26), .in27(x27), .in28(x28), .in29(x29), .in30(x30), .in31(x31), .out(ReadData1), .sel(ReadIndex1));
  Multiplexer #(.select(5), .width(32)) multiplexer_2 (
    .in0({32{1'b0}}), .in1(ra), .in2(sp), .in3(x3), .in4(x4), .in5(t0), .in6(t1), .in7(t2), .in8(s0),
    .in9(s1), .in10(a0), .in11(x11), .in12(x12), .in13(x13), .in14(x14), .in15(x15), .in16(x16), .in17(x17),
    .in18(x18), .in19(x19), .in20(x20), .in21(x21), .in22(x22), .in23(x23), .in24(x24), .in25(x25),
    .in26(x26), .in27(x27), .in28(x28), .in29(x29), .in30(x30), .in31(x31), .out(ReadData2), .sel(ReadIndex2));
  Demultiplexer #(.select(5)) demultiplexer_1 (
    .out1(r1), .out2(r2), .out3(r3), .out4(r4), .out5(r5), .out6(r6), .out7(r7), .out8(r8), .out9(r9),
    .out10(r10), .out11(r11), .out12(r12), .out13(r13), .out14(r14), .out15(r15), .out16(r16), .out17(r17),
    .out18(r18), .out19(r19), .out20(r20), .out21(r21), .out22(r22), .out23(r23), .out24(r24), .out25(r25),
    .out26(r26), .out27(r27), .out28(r28), .out29(r29), .out30(r30), .out31(r31), .in(RegWEn),
    .sel(WriteIndex));  // open: out0

  // Notes on the sheet:
  //   INPUTS to your circuit
  //   DON'T CHANGE THE LOCATIONS OF THE INPUTS AND OUTPUTS!
  //   These are DEBUG/TEST outputs from your circuit.
  //   OUTPUTS from your circuit
endmodule
